# Fritzing sketch v3 (saved by Fritzing 0.8.3b)
circuit board: 13.6cm x 6.8cm
breadboards: 1

parts:
  LED1 = Bicolor 8x8 LED Matrix with I2C backpack
  LED2 = Bicolor 8x8 LED Matrix with I2C backpack
  LED3 = Bicolor 8x8 LED Matrix with I2C backpack
  ARDUINO = Arduino Micro (Rev3)

nets:
  N1: LED1.+, LED2.+, LED3.+, ARDUINO.5V
  N2: LED1.-, LED2.-, LED3.-, ARDUINO.GND
  N3: LED1.D, LED2.D, LED3.D, ARDUINO.D2/SDA
  N4: LED1.C, LED2.C, LED3.C, ARDUINO.D3/SCL
